# Fritzing sketch raspberry_schema (saved by Fritzing 0.9.2b)
breadboards: 1

parts:
  R1 = Resistor [tolerance=±5% resistance=1k package=THT]
  S1 = Pushbutton [package="[THT]"]
  Raspberry_Pi1 = Raspberry Pi 2
  LED1 = LED - 5mm [color="Red (633nm)" package="5 mm [THT]"]
  R2 = Resistor [tolerance=±5% resistance=10k package=THT]

nets:
  N1: R1.Pin_0, Raspberry_Pi1.3v3
  N2: R1.Pin_1, S1.Pin_1, S1.Pin_2, Raspberry_Pi1.GPIO21
  N3: S1.Pin_3, S1.Pin_4, Raspberry_Pi1.GND, LED1.cathode
  N4: Raspberry_Pi1.GPIO6, R2.Pin_1
  N5: LED1.anode, R2.Pin_0
